// Logisim project eg1.circ as structural Verilog: 8 circuits, main circuit main
module main (
  input  in_1,
  output out_2,
  output out_3
);

  not not_1 (out_2, out_3);
  not not_2 (out_3, out_2);
endmodule

module \S_R锁存器  (
  input  in_1,
  input  in_2,
  output out_3,
  output out_4
);

  wire or_1_out, or_2_out;

  or or_1 (or_1_out, in_1, out_4);
  or or_2 (or_2_out, out_3, in_2);
  not not_1 (out_3, or_1_out);
  not not_2 (out_4, or_2_out);
endmodule

module \D锁存器  (
  input  CLK,
  input  in_2,
  output out_3,
  output out_4
);

  wire and_1_out, and_2_out, not_1_out;

  and and_1 (and_1_out, CLK, not_1_out);
  not not_1 (not_1_out, in_2);
  and and_2 (and_2_out, CLK, in_2);
  \S_R锁存器  \s_r锁存器_1  (.in_1(and_1_out), .in_2(and_2_out), .out_3(out_3), .out_4(out_4));
endmodule

module \D触发器  (
  input  in_1,
  input  D,
  output Q,
  output out_4
);

  wire \d锁存器_1_out_3 , not_1_out;

  not not_1 (not_1_out, in_1);
  \D锁存器  \d锁存器_1  (.in_2(D), .out_3(\d锁存器_1_out_3 ), .CLK(not_1_out));  // open: out_4
  \D锁存器  \d锁存器_2  (.in_2(\d锁存器_1_out_3 ), .out_3(Q), .out_4(out_4), .CLK(in_1));
endmodule

module \同步复位  (
  input  D,
  input  reset,
  output Q,
  output out_4
);

  wire and_1_out, clock_1_out, \d锁存器_1_out_3 , not_1_out;

  Clock clock_1 (.out(clock_1_out));
  not not_1 (not_1_out, clock_1_out);
  and and_1 (and_1_out, D, reset);
  \D锁存器  \d锁存器_1  (.in_2(and_1_out), .out_3(\d锁存器_1_out_3 ), .CLK(not_1_out));  // open: out_4
  \D锁存器  \d锁存器_2  (.in_2(\d锁存器_1_out_3 ), .out_3(Q), .out_4(out_4), .CLK(clock_1_out));
endmodule

module \异步复位  (
  input  D,
  input  reset,
  output Q,
  output out_4
);

  wire clock_1_out, \d锁存器_1_out_3 , not_1_out;

  Clock clock_1 (.out(clock_1_out));
  not not_1 (not_1_out, clock_1_out);
  \D锁存器  \d锁存器_1  (.in_2(D), .out_3(\d锁存器_1_out_3 ), .CLK(not_1_out));  // open: out_4
  \D锁存器  \d锁存器_2  (.out_3(Q), .out_4(out_4), .CLK(clock_1_out));  // open: in_2
endmodule

module \搭建寄存器  (
  input  [3:0] in_1,
  input  in_2,
  input  reset,
  input  [3:0] in_4
);

  wire and_1_out, and_2_out, and_3_out, and_4_out;

  and and_1 (and_1_out, reset, in_4[0]);
  and and_2 (and_2_out, reset, in_4[1]);
  and and_3 (and_3_out, reset, in_4[2]);
  and and_4 (and_4_out, reset, in_4[3]);
  \D触发器  \d触发器_1  (.in_1(in_2), .D(and_1_out), .Q(in_1[0]));  // open: out_4
  \D触发器  \d触发器_2  (.in_1(in_2), .D(and_2_out), .Q(in_1[1]));  // open: out_4
  \D触发器  \d触发器_3  (.in_1(in_2), .D(and_3_out), .Q(in_1[2]));  // open: out_4
  \D触发器  \d触发器_4  (.in_1(in_2), .D(and_4_out), .Q(in_1[3]));  // open: out_4
endmodule

module \搭建时序电路  (
);

  wire clock_1_out;

  Clock clock_1 (.out(clock_1_out));
  \搭建寄存器  \u_搭建寄存器_1  (.in_2(clock_1_out));  // open: reset, in_4, in_1
endmodule
